// Logisim project CAO.circ as structural Verilog: 11 circuits, main circuit main
module main (
  input  CounterEnable,
  input  CountEnable,
  input  OEtestdata,
  input  [17:0] TestingData,
  input  [12:0] TestData,
  input  OeTestingData,
  input  WEmar,
  input  OEmar,
  input  WEram,
  input  InternalOE,
  input  OEram,
  input  WEir,
  input  OEir,
  input  WEmbr,
  input  OEmbr,
  input  WEA,
  input  WEor,
  input  OEor,
  input  WEB,
  input  StepEnable,
  output [12:0] CounterContent,
  output [12:0] MARcontent,
  output [17:0] RegIRContent,
  output [17:0] out_24,
  output [17:0] MBRcontent,
  output [17:0] RegAContent,
  output [17:0] AluResult,
  output [17:0] out_28,
  output [17:0] RegBContent,
  output [3:0] ContentOfStepCounter
);

  wire clock_1_out, IorD;
  wire [2:2] OPcode;
  wire [12:0] AO, controlled_buffer_4_out;
  wire [15:0] DO;
  wire [15:13] InstructionRegister_dout;

  Clock clock_1 (.out(clock_1_out));
  Counter #(.max('h1fff), .width(13)) ProgramCounter (
    .count(CountEnable), .clk(clock_1_out), .D(AO), .Q(CounterContent));  // open: clr, load, up, carry
  Register18bits InstructionRegister (
    .Din(AluResult), .WE(WEir), .Clock(clock_1_out), .OE(OEir), .StoredData(RegIRContent),
    .Dout({IorD, OPcode[2], InstructionRegister_dout, AO}));
  assign AO = CounterEnable ? CounterContent : 13'bz;  // Controlled_Buffer controlled_buffer_1
  Decoder #(.select(4)) decoder_1 (
    .out0(DO[15]), .out1(DO[14]), .out2(DO[13]), .out3(DO[12]), .out4(DO[11]), .out5(DO[10]), .out6(DO[9]),
    .out7(DO[8]), .out8(DO[7]), .out9(DO[6]), .out10(DO[5]), .out11(DO[4]), .out12(DO[3]), .out13(DO[2]),
    .out14(DO[1]), .out15(DO[0]), .sel({OPcode[2], InstructionRegister_dout}));  // open: en
  Register18bits DR1 (.Din(AluResult), .WE(WEA), .Clock(clock_1_out), .StoredData(RegAContent));  // open: OE, Dout
  // ALU_18bit alu_18bit_1: pin names not known; wires that end beside it: RegAContent, RegBContent, {3{OPcode[2]}}, AluResult
  Register18bits RegisterB (
    .Din(AluResult), .WE(WEB), .Clock(clock_1_out), .StoredData(RegBContent));  // open: OE, Dout
  LED D8 (.in(AluResult[8]));
  LED D17 (.in(AluResult[17]));
  LED D7 (.in(AluResult[7]));
  LED D6 (.in(AluResult[6]));
  LED D5 (.in(AluResult[5]));
  LED D16 (.in(AluResult[16]));
  LED D15 (.in(AluResult[15]));
  LED D14 (.in(AluResult[14]));
  assign AluResult = OeTestingData ? TestingData : 18'bz;  // Controlled_Buffer controlled_buffer_2
  LED D4 (.in(AluResult[4]));
  LED D3 (.in(AluResult[3]));
  LED D13 (.in(AluResult[13]));
  LED D12 (.in(AluResult[12]));
  LED D2 (.in(AluResult[2]));
  LED D1 (.in(AluResult[1]));
  LED D0 (.in(AluResult[0]));
  LED D11 (.in(AluResult[11]));
  LED D10 (.in(AluResult[10]));
  LED D9 (.in(AluResult[9]));
  assign AluResult = InternalOE ? MBRcontent : 18'bz;  // Controlled_Buffer controlled_buffer_3
  assign controlled_buffer_4_out = OEtestdata ? TestData : 13'bz;  // Controlled_Buffer controlled_buffer_4
  MAR13bits mar13bits_1 (
    .Din(AO), .WE(WEmar), .Clock(clock_1_out), .OE(OEmar), .StoredData(MARcontent),
    .Dout(controlled_buffer_4_out));
  Register18bits MBR (
    .Din(AluResult), .WE(WEmbr), .Clock(clock_1_out), .OE(OEmbr), .StoredData(MBRcontent), .Dout(AluResult));
  Register18bits OutputRegister (
    .Din(AluResult), .WE(WEor), .Clock(clock_1_out), .OE(OEor), .StoredData(out_28), .Dout(AluResult));
  LED l8 (.in(AluResult[8]));
  LED l17 (.in(AluResult[17]));
  LED l7 (.in(AluResult[7]));
  LED l6 (.in(AluResult[6]));
  LED l5 (.in(AluResult[5]));
  LED l16 (.in(AluResult[16]));
  LED l15 (.in(AluResult[15]));
  LED l14 (.in(AluResult[14]));
  LED l4 (.in(AluResult[4]));
  LED l3 (.in(AluResult[3]));
  LED l2 (.in(AluResult[2]));
  LED l13 (.in(AluResult[13]));
  LED l12 (.in(AluResult[12]));
  LED l11 (.in(AluResult[11]));
  LED l1 (.in(AluResult[1]));
  LED l0 (.in(AluResult[0]));
  LED l10 (.in(AluResult[10]));
  LED l9 (.in(AluResult[9]));
  RAM #(.addrWidth(13), .dataWidth(18)) ram_1 (
    .addr({controlled_buffer_4_out[0], controlled_buffer_4_out[1], controlled_buffer_4_out[2], controlled_buffer_4_out[3], controlled_buffer_4_out[4], controlled_buffer_4_out[5], controlled_buffer_4_out[6], controlled_buffer_4_out[7], controlled_buffer_4_out[8], controlled_buffer_4_out[9], controlled_buffer_4_out[10], controlled_buffer_4_out[11], controlled_buffer_4_out[12]}),
    .we(WEram), .oe(OEram), .clk(clock_1_out), .din(AluResult), .dout(AluResult));
  Counter #(.max('hf), .width(4)) SequenceCounter (
    .count(StepEnable), .clk(clock_1_out), .Q(ContentOfStepCounter));  // open: clr, load, up, D, carry

  assign out_24 = AluResult;

  // Other names for the same wires on the sheet: OPcode[1:0] = {2{OPcode[2]}}

  // Notes on the sheet:
  //   Internal Address Bus (13 bits)
  //   Internal Data Bus
  //   External Address Bus (13 bits)
  //   External Data Bus
endmodule

module MemoryCell (
  input  CLK,
  input  WE,
  input  Din,
  input  OE,
  input  RST,
  output Dout,
  output StoredData
);

  wire and_1_out, and_2_out, not_1_out, or_1_out;

  not not_1 (not_1_out, WE);
  and and_1 (and_1_out, StoredData, not_1_out);
  and and_2 (and_2_out, WE, Din);
  or or_1 (or_1_out, and_1_out, and_2_out);
  D_Flip_Flop d_ff_1 (.D(or_1_out), .clk(CLK), .Q(StoredData), .reset(RST));  // open: Qn, preset
  assign Dout = OE ? StoredData : 1'bz;  // Controlled_Buffer controlled_buffer_1

  // Notes on the sheet:
  //   Memory Cell
endmodule

module Register18bits (
  input  WE,
  input  Clock,
  input  OE,
  input  [17:0] Din,
  output [17:0] StoredData,
  output [17:0] Dout
);

  MemoryCell R1 (.WE(WE), .Din(Din[0]), .OE(OE), .CLK(Clock), .Dout(Dout[0]), .StoredData(StoredData[0]));  // open: RST
  MemoryCell R2 (.WE(WE), .Din(Din[1]), .OE(OE), .CLK(Clock), .Dout(Dout[1]), .StoredData(StoredData[1]));  // open: RST
  MemoryCell R3 (.WE(WE), .Din(Din[2]), .OE(OE), .CLK(Clock), .Dout(Dout[2]), .StoredData(StoredData[2]));  // open: RST
  MemoryCell R4 (.WE(WE), .Din(Din[3]), .OE(OE), .CLK(Clock), .Dout(Dout[3]), .StoredData(StoredData[3]));  // open: RST
  MemoryCell R5 (.WE(WE), .Din(Din[4]), .OE(OE), .CLK(Clock), .Dout(Dout[4]), .StoredData(StoredData[4]));  // open: RST
  MemoryCell R6 (.WE(WE), .Din(Din[5]), .OE(OE), .CLK(Clock), .Dout(Dout[5]), .StoredData(StoredData[5]));  // open: RST
  MemoryCell R7 (.WE(WE), .Din(Din[6]), .OE(OE), .CLK(Clock), .Dout(Dout[6]), .StoredData(StoredData[6]));  // open: RST
  MemoryCell R8 (.WE(WE), .Din(Din[7]), .OE(OE), .CLK(Clock), .Dout(Dout[7]), .StoredData(StoredData[7]));  // open: RST
  MemoryCell R9 (.WE(WE), .Din(Din[8]), .OE(OE), .CLK(Clock), .Dout(Dout[8]), .StoredData(StoredData[8]));  // open: RST
  MemoryCell R10 (
    .WE(WE), .Din(Din[9]), .OE(OE), .CLK(Clock), .Dout(Dout[9]), .StoredData(StoredData[9]));  // open: RST
  MemoryCell R11 (
    .WE(WE), .Din(Din[10]), .OE(OE), .CLK(Clock), .Dout(Dout[10]), .StoredData(StoredData[10]));  // open: RST
  MemoryCell R12 (
    .WE(WE), .Din(Din[11]), .OE(OE), .CLK(Clock), .Dout(Dout[11]), .StoredData(StoredData[11]));  // open: RST
  MemoryCell R13 (
    .WE(WE), .Din(Din[12]), .OE(OE), .CLK(Clock), .Dout(Dout[12]), .StoredData(StoredData[12]));  // open: RST
  MemoryCell R14 (
    .WE(WE), .Din(Din[13]), .OE(OE), .CLK(Clock), .Dout(Dout[13]), .StoredData(StoredData[13]));  // open: RST
  MemoryCell R15 (
    .WE(WE), .Din(Din[14]), .OE(OE), .CLK(Clock), .Dout(Dout[14]), .StoredData(StoredData[14]));  // open: RST
  MemoryCell R16 (
    .WE(WE), .Din(Din[15]), .OE(OE), .CLK(Clock), .Dout(Dout[15]), .StoredData(StoredData[15]));  // open: RST
  MemoryCell R17 (
    .WE(WE), .Din(Din[16]), .OE(OE), .CLK(Clock), .Dout(Dout[16]), .StoredData(StoredData[16]));  // open: RST
  MemoryCell R18 (
    .WE(WE), .Din(Din[17]), .OE(OE), .CLK(Clock), .Dout(Dout[17]), .StoredData(StoredData[17]));  // open: RST

  // Notes on the sheet:
  //   Register 18 Bits
endmodule

module MAR13bits (
  input  WE,
  input  Clock,
  input  OE,
  input  [12:0] Din,
  output [12:0] StoredData,
  output [12:0] Dout
);

  MemoryCell R1 (.WE(WE), .Din(Din[0]), .OE(OE), .CLK(Clock), .Dout(Dout[0]), .StoredData(StoredData[0]));  // open: RST
  MemoryCell R2 (.WE(WE), .Din(Din[1]), .OE(OE), .CLK(Clock), .Dout(Dout[1]), .StoredData(StoredData[1]));  // open: RST
  MemoryCell R3 (.WE(WE), .Din(Din[2]), .OE(OE), .CLK(Clock), .Dout(Dout[2]), .StoredData(StoredData[2]));  // open: RST
  MemoryCell R4 (.WE(WE), .Din(Din[3]), .OE(OE), .CLK(Clock), .Dout(Dout[3]), .StoredData(StoredData[3]));  // open: RST
  MemoryCell R5 (.WE(WE), .Din(Din[4]), .OE(OE), .CLK(Clock), .Dout(Dout[4]), .StoredData(StoredData[4]));  // open: RST
  MemoryCell R6 (.WE(WE), .Din(Din[5]), .OE(OE), .CLK(Clock), .Dout(Dout[5]), .StoredData(StoredData[5]));  // open: RST
  MemoryCell R7 (.WE(WE), .Din(Din[6]), .OE(OE), .CLK(Clock), .Dout(Dout[6]), .StoredData(StoredData[6]));  // open: RST
  MemoryCell R8 (.WE(WE), .Din(Din[7]), .OE(OE), .CLK(Clock), .Dout(Dout[7]), .StoredData(StoredData[7]));  // open: RST
  MemoryCell R9 (.WE(WE), .Din(Din[8]), .OE(OE), .CLK(Clock), .Dout(Dout[8]), .StoredData(StoredData[8]));  // open: RST
  MemoryCell R10 (
    .WE(WE), .Din(Din[9]), .OE(OE), .CLK(Clock), .Dout(Dout[9]), .StoredData(StoredData[9]));  // open: RST
  MemoryCell R11 (
    .WE(WE), .Din(Din[10]), .OE(OE), .CLK(Clock), .Dout(Dout[10]), .StoredData(StoredData[10]));  // open: RST
  MemoryCell R12 (
    .WE(WE), .Din(Din[11]), .OE(OE), .CLK(Clock), .Dout(Dout[11]), .StoredData(StoredData[11]));  // open: RST
  MemoryCell R13 (
    .WE(WE), .Din(Din[12]), .OE(OE), .CLK(Clock), .Dout(Dout[12]), .StoredData(StoredData[12]));  // open: RST
endmodule

module Test2 (
  input  CLK,
  input  [17:0] Data,
  input  WE,
  output [17:0] DO
);

  Register #(.width(18)) TR (.D(Data), .en(WE), .clk(CLK), .Q(DO));  // open: clr
  Register #(.width(18)) IR (.D(Data), .en(WE), .clk(CLK), .Q(DO));  // open: clr
  Register #(.width(18)) AC (.D(Data), .en(WE), .clk(CLK), .Q(DO));  // open: clr
  Register #(.width(18)) DR (.D(Data), .en(WE), .clk(CLK), .Q(DO));  // open: clr
endmodule

module Test (
  input  in_1,
  input  in_2,
  input  in_3,
  input  WeIR
);

  wire undriven, undriven_2;
  wire [3:0] counter_1_q;
  wire [15:0] SCO;
  wire [17:0] bitselector_1_out, InstructionRegister_q, undriven_3;

  Clock clock_1 ();  // open: out
  Counter #(.max('hf), .width(4)) counter_1 (
    .clr(in_1), .up(in_2), .clk(undriven), .Q(counter_1_q));  // open: load, count, D, carry
  Decoder #(.select(4)) decoder_1 (
    .out0(SCO[15]), .out1(SCO[14]), .out2(SCO[13]), .out3(SCO[12]), .out4(SCO[11]), .out5(SCO[10]),
    .out6(SCO[9]), .out7(SCO[8]), .out8(SCO[7]), .out9(SCO[6]), .out10(SCO[5]), .out11(SCO[4]),
    .out12(SCO[3]), .out13(SCO[2]), .out14(SCO[1]), .out15(SCO[0]), .sel(counter_1_q));  // open: en
  Register #(.width(18)) InstructionRegister (
    .D(undriven_3), .en(WeIR), .clk(undriven_2), .Q(InstructionRegister_q));  // open: clr
  BitSelector #(.group(18), .width(18)) bitselector_1 (.in(InstructionRegister_q), .out(bitselector_1_out), .sel(in_3));
endmodule

module ALU (
  input  [17:0] RegA,
  input  [17:0] RegB,
  input  OE,
  output [17:0] Dout,
  output [17:0] AluResult,
  output CarryOut
);

  Adder #(.width(18)) adder_1 (.a(RegA), .b(RegB), .out(AluResult), .cout(CarryOut));  // open: cin
  assign Dout = OE ? AluResult : 18'bz;  // Controlled_Buffer controlled_buffer_1

  // Notes on the sheet:
  //   ALU 18bit
endmodule

module DecimalDecoder (
  input  [12:0] Din,
  output [17:0] Dout
);

  ROM #(.addrWidth(13), .dataWidth(18)) rom_1 (
    .addr(Din), .data({Dout[17:15], Dout[11:9], Dout[14:12], Dout[5:3], Dout[8:6], Dout[2:0]}));

  // Notes on the sheet:
  //   contents of rom_1 (hex, n*v repeats v):
  //   e7 21 cb 6b 2d 6e ee 23 ef 2f 21e7 2121 21cb 216b 212d 216e 21ee 2123 21ef 212f cbe7 cb21 cbcb cb6b
  //   cb2d cb6e cbee cb23 cbef cb2f 6be7 6b21 6bcb 6b6b 6b2d 6b6e 6bee 6b23 6bef 6b2f 2de7 2d21 2dcb 2d6b
  //   2d2d 2d6e 2dee 2d23 2def 2d2f 6ee7 6e21 6ecb 6e6b 6e2d 6e6e 6eee 6e23 6eef 6e2f eee7 ee21 eecb ee6b
  //   ee2d ee6e eeee ee23 eeef ee2f 23e7 2321 23cb 236b 232d 236e 23ee 2323 23ef 232f efe7 ef21 efcb ef6b
  //   ef2d ef6e efee ef23 efef ef2f 2fe7 2f21 2fcb 2f6b 2f2d 2f6e 2fee 2f23 2fef 2f2f 1e7e7 1e721 1e7cb
  //   1e76b 1e72d 1e76e 1e7ee 1e723 1e7ef 1e72f 121e7 12121 121cb 1216b 1212d 1216e 121ee 12123 121ef
  //   1212f 1cbe7 1cb21 1cbcb 1cb6b 1cb2d 1cb6e 1cbee 1cb23 1cbef 1cb2f 16be7 16b21 16bcb 16b6b 16b2d
  //   16b6e 16bee 16b23 16bef 16b2f 12de7 12d21 12dcb 12d6b 12d2d 12d6e 12dee 12d23 12def 12d2f 16ee7
  //   16e21 16ecb 16e6b 16e2d 16e6e 16eee 16e23 16eef 16e2f 1eee7 1ee21 1eecb 1ee6b 1ee2d 1ee6e 1eeee
  //   1ee23 1eeef 1ee2f 123e7 12321 123cb 1236b 1232d 1236e 123ee 12323 123ef 1232f 1efe7 1ef21 1efcb
  //   1ef6b 1ef2d 1ef6e 1efee 1ef23 1efef 1ef2f 12fe7 12f21 12fcb 12f6b 12f2d 12f6e 12fee 12f23 12fef
  //   12f2f 3e7e7 3e721 3e7cb 3e76b 3e72d 3e76e 3e7ee 3e723 3e7ef 3e72f 321e7 32121 321cb 3216b 3212d
  //   3216e 321ee 32123 321ef 3212f 3cbe7 3cb21 3cbcb 3cb6b 3cb2d 3cb6e 3cbee 3cb23 3cbef 3cb2f 36be7
  //   36b21 36bcb 36b6b 36b2d 36b6e 36bee 36b23 36bef 36b2f 32de7 32d21 32dcb 32d6b 32d2d 32d6e 32dee
  //   32d23 32def 32d2f 36ee7 36e21 36ecb 36e6b 36e2d 36e6e
  //   Decimal Decoder
endmodule

module ALU1bit (
  input  Carry_in,
  input  Ax,
  input  Bx,
  input  [1:0] Operation,
  output Carry_out,
  output Result
);

  wire ADD, AND, OR, XOR;

  Multiplexer #(.enable("true"), .select(2)) multiplexer_1 (
    .in0(ADD), .in1(AND), .in2(OR), .in3(XOR), .out(Result), .sel(Operation));  // open: en
  and and_1 (AND, Bx, Ax);
  or or_1 (OR, Bx, Ax);
  Adder1bit adder1bit_1 (.b(Ax), .ci(Carry_in), .a(Bx), .co(Carry_out), .s(ADD));
  xor xor_1 (XOR, Ax, Bx);
endmodule

module Adder1bit (
  input  ci,
  input  a,
  input  b,
  output s,
  output co
);

  wire and_1_out, and_2_out, and_3_out, xor_1_out;

  and and_1 (and_1_out, a, b);
  and and_2 (and_2_out, a, ci);
  or or_1 (co, and_1_out, and_2_out, and_3_out);
  and and_3 (and_3_out, b, ci);
  xor xor_1 (xor_1_out, a, b);
  xor xor_2 (s, xor_1_out, ci);
endmodule

module ALU_18bit (
  input  [17:0] A,
  input  [17:0] B,
  input  [1:0] ChooseOperation,
  output [17:0] Output,
  output carry_out
);

  wire alu1bit_1_carry_out, alu1bit_2_carry_out, alu1bit_3_carry_out, alu1bit_4_carry_out,
       alu1bit_5_carry_out, alu1bit_6_carry_out, alu1bit_7_carry_out, alu1bit_8_carry_out,
       alu1bit_9_carry_out, alu1bit_10_carry_out, alu1bit_11_carry_out, alu1bit_12_carry_out,
       alu1bit_13_carry_out, alu1bit_14_carry_out, alu1bit_15_carry_out, alu1bit_16_carry_out,
       alu1bit_17_carry_out;

  ALU1bit alu1bit_1 (
    .Bx(B[0]), .Operation(ChooseOperation), .Ax(A[0]), .Carry_in(1'b0), .Result(Output[0]),
    .Carry_out(alu1bit_1_carry_out));
  ALU1bit alu1bit_2 (
    .Bx(B[1]), .Operation(ChooseOperation), .Ax(A[1]), .Carry_in(alu1bit_1_carry_out), .Result(Output[1]),
    .Carry_out(alu1bit_2_carry_out));
  ALU1bit alu1bit_3 (
    .Bx(B[2]), .Operation(ChooseOperation), .Ax(A[2]), .Carry_in(alu1bit_2_carry_out), .Result(Output[2]),
    .Carry_out(alu1bit_3_carry_out));
  ALU1bit alu1bit_4 (
    .Bx(B[3]), .Operation(ChooseOperation), .Ax(A[3]), .Carry_in(alu1bit_3_carry_out), .Result(Output[3]),
    .Carry_out(alu1bit_4_carry_out));
  ALU1bit alu1bit_5 (
    .Bx(B[4]), .Operation(ChooseOperation), .Ax(A[4]), .Carry_in(alu1bit_4_carry_out), .Result(Output[4]),
    .Carry_out(alu1bit_5_carry_out));
  ALU1bit alu1bit_6 (
    .Bx(B[5]), .Operation(ChooseOperation), .Ax(A[5]), .Carry_in(alu1bit_5_carry_out), .Result(Output[5]),
    .Carry_out(alu1bit_6_carry_out));
  ALU1bit alu1bit_7 (
    .Bx(B[6]), .Operation(ChooseOperation), .Ax(A[6]), .Carry_in(alu1bit_6_carry_out), .Result(Output[6]),
    .Carry_out(alu1bit_7_carry_out));
  ALU1bit alu1bit_8 (
    .Bx(B[7]), .Operation(ChooseOperation), .Ax(A[7]), .Carry_in(alu1bit_7_carry_out), .Result(Output[7]),
    .Carry_out(alu1bit_8_carry_out));
  ALU1bit alu1bit_9 (
    .Bx(B[8]), .Operation(ChooseOperation), .Ax(A[8]), .Carry_in(alu1bit_8_carry_out), .Result(Output[8]),
    .Carry_out(alu1bit_9_carry_out));
  ALU1bit alu1bit_10 (
    .Bx(A[9]), .Operation(ChooseOperation), .Ax(B[9]), .Carry_in(alu1bit_9_carry_out), .Result(Output[9]),
    .Carry_out(alu1bit_10_carry_out));
  ALU1bit alu1bit_11 (
    .Bx(B[10]), .Operation(ChooseOperation), .Ax(A[10]), .Carry_in(alu1bit_10_carry_out),
    .Result(Output[10]), .Carry_out(alu1bit_11_carry_out));
  ALU1bit alu1bit_12 (
    .Bx(B[11]), .Operation(ChooseOperation), .Ax(A[11]), .Carry_in(alu1bit_11_carry_out),
    .Result(Output[11]), .Carry_out(alu1bit_12_carry_out));
  ALU1bit alu1bit_13 (
    .Bx(B[12]), .Operation(ChooseOperation), .Ax(A[12]), .Carry_in(alu1bit_12_carry_out),
    .Result(Output[12]), .Carry_out(alu1bit_13_carry_out));
  ALU1bit alu1bit_14 (
    .Bx(B[13]), .Operation(ChooseOperation), .Ax(A[13]), .Carry_in(alu1bit_13_carry_out),
    .Result(Output[13]), .Carry_out(alu1bit_14_carry_out));
  ALU1bit alu1bit_15 (
    .Bx(B[14]), .Operation(ChooseOperation), .Ax(A[14]), .Carry_in(alu1bit_14_carry_out),
    .Result(Output[14]), .Carry_out(alu1bit_15_carry_out));
  ALU1bit alu1bit_16 (
    .Bx(B[15]), .Operation(ChooseOperation), .Ax(A[15]), .Carry_in(alu1bit_15_carry_out),
    .Result(Output[15]), .Carry_out(alu1bit_16_carry_out));
  ALU1bit alu1bit_17 (
    .Bx(B[16]), .Operation(ChooseOperation), .Ax(A[16]), .Carry_in(alu1bit_16_carry_out),
    .Result(Output[16]), .Carry_out(alu1bit_17_carry_out));
  ALU1bit alu1bit_18 (
    .Bx(B[17]), .Operation(ChooseOperation), .Ax(A[17]), .Carry_in(alu1bit_17_carry_out),
    .Result(Output[17]), .Carry_out(carry_out));
endmodule
